// Logisim project 1.circ as structural Verilog: 5 circuits, main circuit main
module main (
  input  [3:0] in_1,
  input  _8,
  input  _4,
  input  _2,
  input  _1,
  input  [2:0] in_6,
  input  [1:0] A,
  input  [1:0] B
);

  wire alpha_7seg_decoder_1_out_4, alpha_7seg_decoder_1_out_5, alpha_7seg_decoder_1_out_6,
       alpha_7seg_decoder_1_out_7, alpha_7seg_decoder_1_out_8, alpha_7seg_decoder_1_out_9,
       alpha_7seg_decoder_1_out_10, bcd_7seg_decoder_1_out_5, bcd_7seg_decoder_1_out_6,
       bcd_7seg_decoder_1_out_7, bcd_7seg_decoder_1_out_8, bcd_7seg_decoder_1_out_9,
       bcd_7seg_decoder_1_out_10, bcd_7seg_decoder_1_out_11, bcd_7seg_decoder_2_out_5,
       bcd_7seg_decoder_2_out_6, bcd_7seg_decoder_2_out_7, bcd_7seg_decoder_2_out_8,
       bcd_7seg_decoder_2_out_9, bcd_7seg_decoder_2_out_10, bcd_7seg_decoder_2_out_11,
       bcd_7seg_decoder_3_out_5, bcd_7seg_decoder_3_out_6, bcd_7seg_decoder_3_out_7,
       bcd_7seg_decoder_3_out_8, bcd_7seg_decoder_3_out_9, bcd_7seg_decoder_3_out_10,
       bcd_7seg_decoder_3_out_11, n2_bit_comparator_1_out_5, n2_bit_comparator_1_out_6,
       n2_bit_comparator_1_out_7, n2_bit_comparator_1_out_8, n2_bit_comparator_1_out_9,
       n2_bit_comparator_1_out_10, n2_bit_comparator_1_out_11, \ทว_ค_ณ_1_out_5 , \ทว_ค_ณ_1_out_6 ,
       \ทว_ค_ณ_1_out_7 , \ทว_ค_ณ_1_out_8 , \ทว_ค_ณ_1_out_9 , \ทว_ค_ณ_1_out_10 , \ทว_ค_ณ_1_out_11 ,
       \ทว_ค_ณ_1_out_12 ;

  \ทว_ค_ณ  \u_ทว_ค_ณ_1  (
    .in_1(_8), .in_2(_4), .in_3(_2), .in_4(_1), .out_5(\ทว_ค_ณ_1_out_5 ), .out_6(\ทว_ค_ณ_1_out_6 ),
    .out_7(\ทว_ค_ณ_1_out_7 ), .out_8(\ทว_ค_ณ_1_out_8 ), .out_9(\ทว_ค_ณ_1_out_9 ), .out_10(\ทว_ค_ณ_1_out_10 ),
    .out_11(\ทว_ค_ณ_1_out_11 ), .out_12(\ทว_ค_ณ_1_out_12 ));
  BCD_7Seg_Decoder bcd_7seg_decoder_1 (
    .A(\ทว_ค_ณ_1_out_8 ), .B(\ทว_ค_ณ_1_out_7 ), .C(\ทว_ค_ณ_1_out_6 ), .D(\ทว_ค_ณ_1_out_5 ),
    .out_5(bcd_7seg_decoder_1_out_5), .out_6(bcd_7seg_decoder_1_out_6), .out_7(bcd_7seg_decoder_1_out_7),
    .out_8(bcd_7seg_decoder_1_out_8), .out_9(bcd_7seg_decoder_1_out_9), .out_10(bcd_7seg_decoder_1_out_10),
    .out_11(bcd_7seg_decoder_1_out_11));
  BCD_7Seg_Decoder bcd_7seg_decoder_2 (
    .A(\ทว_ค_ณ_1_out_9 ), .B(\ทว_ค_ณ_1_out_10 ), .C(\ทว_ค_ณ_1_out_11 ), .D(\ทว_ค_ณ_1_out_12 ),
    .out_5(bcd_7seg_decoder_2_out_5), .out_6(bcd_7seg_decoder_2_out_6), .out_7(bcd_7seg_decoder_2_out_7),
    .out_8(bcd_7seg_decoder_2_out_8), .out_9(bcd_7seg_decoder_2_out_9), .out_10(bcd_7seg_decoder_2_out_10),
    .out_11(bcd_7seg_decoder_2_out_11));
  alpha_7Seg_Decoder alpha_7seg_decoder_1 (
    .in_1(in_6[2]), .in_2(in_6[1]), .in_3(in_6[0]), .out_4(alpha_7seg_decoder_1_out_4),
    .out_5(alpha_7seg_decoder_1_out_5), .out_6(alpha_7seg_decoder_1_out_6),
    .out_7(alpha_7seg_decoder_1_out_7), .out_8(alpha_7seg_decoder_1_out_8),
    .out_9(alpha_7seg_decoder_1_out_9), .out_10(alpha_7seg_decoder_1_out_10));
  _2_bit_Comparator u_2_bit_comparator_1 (
    .in_1(A[1]), .in_2(A[0]), .in_3(B[1]), .in_4(B[0]), .out_5(n2_bit_comparator_1_out_5),
    .out_6(n2_bit_comparator_1_out_6), .out_7(n2_bit_comparator_1_out_7), .out_8(n2_bit_comparator_1_out_8),
    .out_9(n2_bit_comparator_1_out_9), .out_10(n2_bit_comparator_1_out_10),
    .out_11(n2_bit_comparator_1_out_11));
  BCD_7Seg_Decoder bcd_7seg_decoder_3 (
    .A(in_1[3]), .B(in_1[2]), .C(in_1[1]), .D(in_1[0]), .out_5(bcd_7seg_decoder_3_out_5),
    .out_6(bcd_7seg_decoder_3_out_6), .out_7(bcd_7seg_decoder_3_out_7), .out_8(bcd_7seg_decoder_3_out_8),
    .out_9(bcd_7seg_decoder_3_out_9), .out_10(bcd_7seg_decoder_3_out_10), .out_11(bcd_7seg_decoder_3_out_11));
  _7_Segment_Display u_7_segment_display_1 (
    .g(bcd_7seg_decoder_1_out_11), .f(bcd_7seg_decoder_1_out_10), .a(bcd_7seg_decoder_1_out_5),
    .b(bcd_7seg_decoder_1_out_6), .e(bcd_7seg_decoder_1_out_9), .d(bcd_7seg_decoder_1_out_8),
    .c(bcd_7seg_decoder_1_out_7));  // open: dp
  _7_Segment_Display u_7_segment_display_2 (
    .g(alpha_7seg_decoder_1_out_4), .f(alpha_7seg_decoder_1_out_5), .a(alpha_7seg_decoder_1_out_10),
    .b(alpha_7seg_decoder_1_out_9), .e(alpha_7seg_decoder_1_out_6), .d(alpha_7seg_decoder_1_out_7),
    .c(alpha_7seg_decoder_1_out_8));  // open: dp
  _7_Segment_Display u_7_segment_display_3 (
    .g(n2_bit_comparator_1_out_5), .f(n2_bit_comparator_1_out_6), .a(n2_bit_comparator_1_out_11),
    .b(n2_bit_comparator_1_out_10), .e(n2_bit_comparator_1_out_7), .d(n2_bit_comparator_1_out_8),
    .c(n2_bit_comparator_1_out_9));  // open: dp
  _7_Segment_Display u_7_segment_display_4 (
    .g(bcd_7seg_decoder_3_out_11), .f(bcd_7seg_decoder_3_out_10), .a(bcd_7seg_decoder_3_out_5),
    .b(bcd_7seg_decoder_3_out_6), .e(bcd_7seg_decoder_3_out_9), .d(bcd_7seg_decoder_3_out_8),
    .c(bcd_7seg_decoder_3_out_7));  // open: dp
  _7_Segment_Display u_7_segment_display_5 (
    .g(bcd_7seg_decoder_2_out_11), .f(bcd_7seg_decoder_2_out_10), .a(bcd_7seg_decoder_2_out_5),
    .b(bcd_7seg_decoder_2_out_6), .e(bcd_7seg_decoder_2_out_9), .d(bcd_7seg_decoder_2_out_8),
    .c(bcd_7seg_decoder_2_out_7));  // open: dp

  // Notes on the sheet:
  //   ทดลอง2
  //   ทดลอง3
  //   ทดลอง1
  //   ทดลอง4
endmodule

module BCD_7Seg_Decoder (
  input  A,
  input  B,
  input  C,
  input  D,
  output out_5,
  output out_6,
  output out_7,
  output out_8,
  output out_9,
  output out_10,
  output out_11
);

  wire and_1_out, and_2_out, and_3_out, and_4_out, and_5_out, and_6_out, and_7_out, and_8_out, and_9_out,
       and_10_out, and_11_out, and_12_out, and_13_out, and_14_out, and_15_out, and_16_out, not_1_out,
       not_2_out, not_3_out, not_4_out;

  not not_1 (not_1_out, A);
  not not_2 (not_2_out, C);
  not not_3 (not_3_out, B);
  not not_4 (not_4_out, D);
  and and_1 (and_1_out, B, D);
  and and_2 (and_2_out, not_2_out, not_3_out, not_4_out);
  and and_3 (and_3_out, not_2_out, not_4_out);
  and and_4 (and_4_out, C, D);
  and and_5 (and_5_out, C, not_4_out);
  and and_6 (and_6_out, not_2_out, D, B);
  and and_7 (and_7_out, not_2_out, not_4_out, not_3_out);
  and and_8 (and_8_out, C, not_1_out, not_3_out);
  and and_9 (and_9_out, C, not_4_out);
  and and_10 (and_10_out, not_2_out, not_4_out, not_3_out);
  and and_11 (and_11_out, B, not_4_out);
  and and_12 (and_12_out, not_2_out, not_4_out);
  and and_13 (and_13_out, not_2_out, B);
  and and_14 (and_14_out, not_2_out, B);
  and and_15 (and_15_out, C, not_4_out);
  and and_16 (and_16_out, C, not_3_out);
  or or_1 (out_5, A, C, and_1_out, and_2_out);
  or or_2 (out_6, not_3_out, A, and_3_out, and_4_out);
  or or_3 (out_7, A, B, not_2_out, D);
  or or_4 (out_8, and_5_out, and_6_out, and_7_out, and_8_out);
  or or_5 (out_9, and_9_out, and_10_out);
  or or_6 (out_10, A, and_11_out, and_12_out, and_13_out);
  or or_7 (out_11, A, and_14_out, and_15_out, and_16_out);
endmodule

module \ทว_ค_ณ  (
  input  in_1,
  input  in_2,
  input  in_3,
  input  in_4,
  output out_5,
  output out_6,
  output out_7,
  output out_8,
  output out_9,
  output out_10,
  output out_11,
  output out_12
);

  wire and_1_out, and_2_out, and_3_out, and_4_out, and_5_out, and_6_out, and_8_out, and_9_out, and_10_out,
       and_11_out, and_12_out, and_13_out, and_14_out, and_15_out, and_16_out, and_17_out, and_18_out,
       and_19_out, not_1_out, not_2_out, not_3_out, not_4_out;

  not not_1 (not_1_out, in_1);
  not not_2 (not_2_out, in_2);
  not not_3 (not_3_out, in_3);
  not not_4 (not_4_out, in_4);
  and and_1 (and_1_out, in_2, in_3, in_4);
  and and_2 (and_2_out, not_1_out, in_2, in_4);
  and and_3 (and_3_out, not_1_out, in_2, in_3);
  and and_4 (and_4_out, in_1, not_2_out, not_3_out);
  and and_5 (and_5_out, in_1, in_2);
  and and_6 (and_6_out, in_1, in_3);
  and and_7 (out_7, in_1, not_1_out);
  and and_8 (and_8_out, not_1_out, not_2_out, in_4);
  and and_9 (and_9_out, in_3, in_4, not_2_out);
  and and_10 (and_10_out, in_1, not_3_out, not_2_out, not_4_out);
  and and_11 (and_11_out, in_1, in_2, not_3_out, in_4);
  and and_12 (and_12_out, not_1_out, in_2, in_3, not_4_out);
  and and_13 (and_13_out, in_3, in_4, not_1_out);
  and and_14 (and_14_out, in_1, in_2, not_3_out);
  and and_15 (and_15_out, not_3_out, not_4_out, in_1);
  and and_16 (and_16_out, not_1_out, not_2_out, in_3);
  and and_17 (and_17_out, not_1_out, in_2, not_3_out, not_4_out);
  and and_18 (and_18_out, in_1, not_2_out, not_3_out, in_4);
  and and_19 (and_19_out, in_1, in_2, in_3, not_4_out);
  or or_1 (out_5, and_1_out, and_2_out, and_3_out, and_4_out);
  or or_2 (out_6, and_5_out, and_6_out);
  or or_3 (out_11, and_8_out, and_9_out, and_10_out, and_11_out, and_12_out);
  or or_4 (out_10, and_13_out, and_14_out, and_15_out, and_16_out);
  or or_5 (out_9, and_17_out, and_18_out, and_19_out);

  assign out_8 = out_7;
  assign out_12 = out_7;
endmodule

module alpha_7Seg_Decoder (
  input  in_1,
  input  in_2,
  input  in_3,
  output out_4,
  output out_5,
  output out_6,
  output out_7,
  output out_8,
  output out_9,
  output out_10
);

  wire and_1_out, and_2_out, and_3_out, and_4_out, and_5_out, and_6_out, not_1_out, not_2_out, not_3_out,
       or_1_out;

  not not_1 (not_1_out, in_1);
  not not_2 (not_2_out, in_3);
  not not_3 (not_3_out, in_2);
  and and_1 (and_1_out, not_1_out, not_3_out);
  or or_1 (or_1_out, not_1_out, not_3_out);
  and and_2 (and_2_out, not_1_out, in_2);
  and and_3 (and_3_out, in_1, not_3_out);
  and and_4 (and_4_out, not_2_out, in_2);
  and and_5 (and_5_out, in_3, not_3_out);
  and and_6 (and_6_out, not_2_out, or_1_out);
  nand nand_1 (out_5, in_1, not_1_out);
  or or_2 (out_7, and_2_out, and_3_out);
  or or_3 (out_4, and_4_out, and_5_out);
  or or_4 (out_8, and_1_out, and_6_out);

  assign out_6 = out_5;
  assign out_9 = out_8;
  assign out_10 = out_5;
endmodule

module _2_bit_Comparator (
  input  in_1,
  input  in_2,
  input  in_3,
  input  in_4,
  output out_5,
  output out_6,
  output out_7,
  output out_8,
  output out_9,
  output out_10,
  output out_11
);

  wire and_1_out, and_2_out, and_3_out, and_4_out, and_5_out, and_6_out, and_7_out, and_8_out, and_9_out,
       not_1_out, not_2_out, not_3_out, not_4_out;

  not not_1 (not_1_out, in_1);
  not not_2 (not_2_out, in_2);
  not not_3 (not_3_out, in_4);
  not not_4 (not_4_out, in_3);
  and and_1 (and_1_out, in_1, not_4_out);
  and and_2 (and_2_out, not_1_out, in_3);
  and and_3 (and_3_out, not_2_out, in_4);
  and and_4 (and_4_out, in_2, not_3_out);
  or or_1 (out_5, in_1, not_1_out);
  and and_5 (and_5_out, not_1_out, in_4);
  and and_6 (and_6_out, in_3, in_4);
  and and_7 (and_7_out, not_1_out, in_3);
  and and_8 (and_8_out, not_2_out, in_3);
  and and_9 (and_9_out, not_1_out, not_2_out);
  or or_2 (out_9, and_1_out, and_2_out, and_3_out, and_4_out);
  or or_3 (out_8, and_5_out, and_6_out, and_7_out, and_8_out, and_9_out);

  assign out_6 = out_5;
  assign out_7 = out_5;
  assign out_10 = out_9;
  assign out_11 = out_5;
endmodule
