// Logisim project 2 bitเทียบ.circ as structural Verilog: 2 circuits, main circuit main
module main (
  input  A1,
  input  A0,
  input  B1,
  input  B0,
  output out_5,
  output out_6,
  output out_7
);

  _2bit u_2bit_1 (.A1(A1), .A0(A0), .B1(B1), .B0(B0), .out_5(out_5), .out_6(out_6), .out_7(out_7));
endmodule

// 2 bit
module _2bit (
  input  A1,
  input  A0,
  input  B1,
  input  B0,
  output out_5,
  output out_6,
  output out_7
);

  wire and_1_out, and_2_out, and_3_out, and_4_out, and_5_out, and_6_out, and_7_out, and_8_out, not_1_out,
       not_2_out, not_3_out, not_4_out;

  not not_1 (not_1_out, A1);
  not not_2 (not_2_out, A0);
  not not_3 (not_3_out, B0);
  not not_4 (not_4_out, B1);
  and and_1 (and_1_out, not_4_out, A1);
  and and_2 (and_2_out, not_4_out, A0);
  and and_3 (and_3_out, not_4_out, not_3_out);
  and and_4 (and_4_out, not_3_out, A1);
  and and_5 (and_5_out, A1, A0);
  or or_1 (out_5, B0, not_3_out);
  or or_2 (out_6, and_1_out, and_2_out, and_3_out, and_4_out, and_5_out);
  and and_6 (and_6_out, not_4_out, A1);
  and and_7 (and_7_out, not_4_out, not_3_out, A0);
  and and_8 (and_8_out, not_3_out, A1, A0);
  or or_3 (out_7, and_6_out, and_7_out, and_8_out);
endmodule
