// Logisim project บวกเลข.circ as structural Verilog: 5 circuits, main circuit main
module main (
  input  in_1,
  input  in_2,
  input  in_3,
  input  in_4,
  input  in_5,
  input  in_6,
  input  in_7,
  input  in_8,
  output out_9,
  output out_10,
  output out_11,
  output out_12
);

  wire adder2_1_out_5, adder2_2_out_5, adder_1_out_4;

  adder adder_1 (.in_1(in_1), .in_2(in_2), .out_3(out_12), .out_4(adder_1_out_4));
  adder2 adder2_1 (.in_1(in_3), .in_2(in_4), .in_3(adder_1_out_4), .out_4(out_11), .out_5(adder2_1_out_5));
  adder2 adder2_2 (.in_1(in_5), .in_2(in_6), .in_3(adder2_1_out_5), .out_4(out_10), .out_5(adder2_2_out_5));
  adder2 adder2_3 (.in_1(in_7), .in_2(in_8), .in_3(adder2_2_out_5), .out_4(out_9));  // open: out_5
endmodule

module adder (
  input  in_1,
  input  in_2,
  output out_3,
  output out_4
);

  xor xor_1 (out_3, in_1, in_2);
  and and_1 (out_4, in_1, in_2);
endmodule

module adder2 (
  input  in_1,
  input  in_2,
  input  in_3,
  output out_4,
  output out_5
);

  wire adder_1_out_3, adder_1_out_4, adder_2_out_4;

  adder adder_1 (.in_1(in_1), .in_2(in_2), .out_3(adder_1_out_3), .out_4(adder_1_out_4));
  adder adder_2 (.in_1(adder_1_out_3), .in_2(in_3), .out_3(out_4), .out_4(adder_2_out_4));
  or or_1 (out_5, adder_2_out_4, adder_1_out_4);
endmodule

module _555 (
  input  [3:0] in_1,
  input  [3:0] in_2
);

  wire de_1_out_5, de_1_out_6, de_1_out_7, de_1_out_8, de_1_out_9, de_1_out_10, de_1_out_11, main_1_out_9,
       main_1_out_10, main_1_out_11, main_1_out_12;

  main main_1 (
    .in_1(in_1[0]), .in_2(in_2[0]), .in_3(in_1[1]), .in_4(in_2[1]), .in_5(in_1[2]), .in_6(in_2[2]),
    .in_7(in_1[3]), .in_8(in_2[3]), .out_9(main_1_out_9), .out_10(main_1_out_10), .out_11(main_1_out_11),
    .out_12(main_1_out_12));
  de de_1 (
    .A(main_1_out_9), .B(main_1_out_10), .C(main_1_out_11), .D(main_1_out_12), .out_5(de_1_out_5),
    .out_6(de_1_out_6), .out_7(de_1_out_7), .out_8(de_1_out_8), .out_9(de_1_out_9), .out_10(de_1_out_10),
    .out_11(de_1_out_11));
  _7_Segment_Display u_7_segment_display_1 (
    .g(de_1_out_11), .f(de_1_out_10), .a(de_1_out_5), .b(de_1_out_6), .e(de_1_out_9), .d(de_1_out_8),
    .c(de_1_out_7));  // open: dp
endmodule

module de (
  input  A,
  input  B,
  input  C,
  input  D,
  output out_5,
  output out_6,
  output out_7,
  output out_8,
  output out_9,
  output out_10,
  output out_11
);

  wire and_1_out, and_2_out, and_3_out, and_4_out, and_5_out, and_6_out, and_7_out, and_8_out, and_9_out,
       and_10_out, and_11_out, and_12_out, and_13_out, and_14_out, and_15_out, and_16_out, not_1_out,
       not_2_out, not_3_out, not_4_out;

  not not_1 (not_1_out, A);
  not not_2 (not_2_out, C);
  not not_3 (not_3_out, B);
  not not_4 (not_4_out, D);
  and and_1 (and_1_out, B, D);
  and and_2 (and_2_out, not_2_out, not_3_out, not_4_out);
  and and_3 (and_3_out, not_2_out, not_4_out);
  and and_4 (and_4_out, C, D);
  and and_5 (and_5_out, C, not_4_out);
  and and_6 (and_6_out, not_2_out, D, B);
  and and_7 (and_7_out, not_2_out, not_4_out, not_3_out);
  and and_8 (and_8_out, C, not_1_out, not_3_out);
  and and_9 (and_9_out, C, not_4_out);
  and and_10 (and_10_out, not_2_out, not_4_out, not_3_out);
  and and_11 (and_11_out, B, not_4_out);
  and and_12 (and_12_out, not_2_out, not_4_out);
  and and_13 (and_13_out, not_2_out, B);
  and and_14 (and_14_out, not_2_out, B);
  and and_15 (and_15_out, C, not_4_out);
  and and_16 (and_16_out, C, not_3_out);
  or or_1 (out_5, A, C, and_1_out, and_2_out);
  or or_2 (out_6, not_3_out, A, and_3_out, and_4_out);
  or or_3 (out_7, A, B, not_2_out, D);
  or or_4 (out_8, and_5_out, and_6_out, and_7_out, and_8_out);
  or or_5 (out_9, and_9_out, and_10_out);
  or or_6 (out_10, A, and_11_out, and_12_out, and_13_out);
  or or_7 (out_11, A, and_14_out, and_15_out, and_16_out);
endmodule
