// Logisim project เพิ่มเลข1.circ as structural Verilog: 2 circuits, main circuit main
module main (
  input  in_1,
  input  in_2,
  input  in_3,
  output out_4,
  output out_5,
  output out_6
);

  _3bit u_3bit_1 (.A(in_1), .B(in_2), .C(in_3), .X(out_6), .Y(out_5), .Z(out_4));
endmodule

module _3bit (
  input  A,
  input  B,
  input  C,
  output X,
  output Y,
  output Z
);

  wire and_1_out, and_2_out, and_3_out, and_4_out, and_5_out, not_1_out, not_2_out;

  not not_1 (not_1_out, A);
  not not_2 (not_2_out, B);
  not not_3 (X, C);
  and and_1 (and_1_out, X, A);
  and and_2 (and_2_out, A, not_2_out);
  and and_3 (and_3_out, not_1_out, B, C);
  and and_4 (and_4_out, X, B);
  and and_5 (and_5_out, C, not_2_out);
  or or_1 (Z, and_1_out, and_2_out, and_3_out);
  or or_2 (Y, and_4_out, and_5_out);
endmodule
